# Fritzing sketch pitch_please_191222 (saved by Fritzing 0.9.3b)
circuit board: 5.34cm x 5.7cm
breadboards: 2

parts:
  RLED30 = Resistor [tolerance=±5% resistance=220 package=THT]
  RLED20 = Resistor [tolerance=±5% resistance=220 package=THT]
  RLED10 = Resistor [tolerance=±5% resistance=220 package=THT]
  RLED00 = Resistor [tolerance=±5% resistance=220 package=THT]
  T0 = npn-Powertransistor [package="TO220 [THT]"]
  RLED01 = Resistor [tolerance=±5% resistance=47 package=THT]
  T1 = npn-Powertransistor [package="TO220 [THT]"]
  T2 = npn-Powertransistor [package="TO220 [THT]"]
  T3 = npn-Powertransistor [package="TO220 [THT]"]
  T4 = npn-Powertransistor [package="TO220 [THT]"]
  T5 = npn-Powertransistor [package="TO220 [THT]"]
  RLED40 = Resistor [tolerance=±5% resistance=220 package=THT]
  RLED50 = Resistor [tolerance=±5% resistance=220 package=THT]
  RLED11 = Resistor [tolerance=±5% resistance=47 package=THT]
  RLED21 = Resistor [tolerance=±5% resistance=47 package=THT]
  RLED31 = Resistor [tolerance=±5% resistance=47 package=THT]
  RLED41 = Resistor [tolerance=±5% resistance=47 package=THT]
  RLED51 = Resistor [tolerance=±5% resistance=47 package=THT]
  B_G_R_+ = screw terminal, 4 pins
  B_G_R_+_2 = screw terminal, 4 pins
  Arduino = Arduino Uno (Rev3)
  STATUS = LED - 5mm [color="Red (633nm)" package="5 mm [THT]"]
  RS = Resistor [tolerance=±5% resistance=220 package=THT]

nets:
  N1: RLED30.Pin_0, Arduino.D11_PWM/MOSI
  N2: RLED30.Pin_1, T3.base
  N3: RLED20.Pin_0, Arduino.D3_PWM
  N4: RLED20.Pin_1, T2.base
  N5: RLED10.Pin_0, Arduino.D5_PWM
  N6: RLED10.Pin_1, T1.base
  N7: RLED00.Pin_0, Arduino.D6_PWM
  N8: RLED00.Pin_1, T0.base
  N9: T0.collector, RLED01.Pin_0
  N10: T0.emitter, T1.emitter, T2.emitter, T3.emitter, T4.emitter, T5.emitter, Arduino.GND, STATUS.cathode
  N11: RLED01.Pin_1, B_G_R_+.pin1
  N12: T1.collector, RLED11.Pin_0
  N13: T2.collector, RLED21.Pin_0
  N14: T3.collector, RLED31.Pin_0
  N15: T4.base, RLED40.Pin_1
  N16: T4.collector, RLED41.Pin_0
  N17: T5.base, RLED50.Pin_1
  N18: T5.collector, RLED51.Pin_0
  N19: RLED40.Pin_0, Arduino.D10_PWM/SS
  N20: RLED50.Pin_0, Arduino.D9_PWM
  N21: RLED11.Pin_1, B_G_R_+.pin2
  N22: RLED21.Pin_1, B_G_R_+.pin3
  N23: RLED31.Pin_1, B_G_R_+_2.pin1
  N24: RLED41.Pin_1, B_G_R_+_2.pin2
  N25: RLED51.Pin_1, B_G_R_+_2.pin3
  N26: B_G_R_+.pin4, B_G_R_+_2.pin4, Arduino.VIN
  N27: Arduino.D8, RS.Pin_1
  N28: STATUS.anode, RS.Pin_0

notes:
  Miroslav Hlava
  MD 2019
  Pitch
  Please!!!
