# Fritzing sketch 250802_v3-0_esp32_dmx (saved by Fritzing 1.0.5)
circuit board: 7.5cm x 4.5cm
breadboards: 3

parts:
  SN74AHCT125 = IC, DIP package, 14 pins [chip_label=SN74AHCT125]
  LED1 = screw terminal, 3 pins
  LED2 = screw terminal, 3 pins
  LED3 = screw terminal, 3 pins
  LED4 = screw terminal, 3 pins
  12+ = Screw terminal - 2 pins [package=THT]
  STPDWN = screw terminal, 3 pins
  Part1 = MAX 485 Module
  DMXOUT = screw terminal, 3 pins
  ESP32 = AZ-Delivery ESP32 NodeMCU DevKit C
  R3 = Resistor [tolerance=±5% power=0.25W resistance=100 package=THT]
  R4 = Resistor [tolerance=±5% power=0.25W resistance=100 package=THT]
  R2 = Resistor [tolerance=±5% power=0.25W resistance=100 package=THT]
  R1 = Resistor [tolerance=±5% power=0.25W resistance=100 package=THT]
  +_12V_- = Screw terminal - 2 pins [package=THT]
  DMXIN = screw terminal, 3 pins
  C4 = Ceramic Capacitor [capacitance=100nF voltage=50V package="200 mil [THT, multilayer]"]
  C3 = Ceramic Capacitor [capacitance=100nF voltage=50V package="200 mil [THT, multilayer]"]
  Part2 = MAX 485 Module
  C1 = Electrolytic Capacitor [capacitance=1µF voltage=35V package="200 mil [THT, electrolytic]"]
  C2 = Electrolytic Capacitor [capacitance=1µF voltage=35V package="200 mil [THT, electrolytic]"]
  +_5V_- = Screw terminal - 2 pins [package=THT]
  C5 = Electrolytic Capacitor [capacitance=10µF voltage=35V package="100 mil [THT, electrolytic]"]

nets:
  GND: SN74AHCT125.pin1, SN74AHCT125.pin4, SN74AHCT125.pin7, SN74AHCT125.pin10, SN74AHCT125.pin13, LED1.pin1, LED2.pin1, LED3.pin1, LED4.pin1, 12+.pin1, STPDWN.pin1, Part1.GND, DMXOUT.pin1, ESP32.GND#12, ESP32.GND#33, +_12V_-.pin1, DMXIN.pin1, C4.1, C3.1, Part2.GND, C1.-, C2.-, +_5V_-.pin1, C5.-
  N1: SN74AHCT125.pin2, ESP32.G21
  N2: SN74AHCT125.pin3, R1.Pin_1
  N3: SN74AHCT125.pin5, ESP32.G19
  N4: SN74AHCT125.pin6, R2.Pin_1
  N5: SN74AHCT125.pin8, R3.Pin_1
  N6: SN74AHCT125.pin9, ESP32.S00, ESP32.G17, ESP32.G35, ESP32.G26
  N7: SN74AHCT125.pin11, R4.Pin_1
  N8: SN74AHCT125.pin12, ESP32.G27
  VCC: SN74AHCT125.pin14, STPDWN.pin2, Part1.VCC, ESP32.V5, C4.0, C3.0, Part2.VCC, C2.+, +_5V_-.pin2
  N9: LED1.pin2, R1.Pin_0
  N10: LED1.pin3, LED2.pin3, LED3.pin3, LED4.pin3, 12+.pin2, STPDWN.pin3, +_12V_-.pin2, C1.+
  N11: LED2.pin2, R2.Pin_0
  N12: LED3.pin2, R3.Pin_0
  N13: LED4.pin2, R4.Pin_0
  N14: Part1.A, DMXIN.pin3
  N15: Part1.B, DMXIN.pin2
  N16: Part1.RO, ESP32.G16, Part2.DI
  N17: Part1.RE, Part1.DE, ESP32.CLK, ESP32.G5, ESP32.G32
  N18: DMXOUT.pin2, Part2.B
  N19: DMXOUT.pin3, Part2.A
  N20: ESP32.EN, C5.+
  N21: ESP32.G33, Part2.RE, Part2.DE

notes:
  VCC D GND
  GND A  B
  PitchPls! v3
  MH 2025

custom parts:
  MAX 485 Module: TTL to MCU module
